# Fritzing sketch Untitled Sketch (saved by Fritzing 0.9.3b)
breadboards: 1

parts:
  Part1 = Arduino Nano (Rev3.0)
  J1 = Camdenboss CTB0158-4 [part_number="GPS BY-GPSV3-NEO" package=THT]
  ZS-042_RTC1 = ZS-042 RTC Module [part_number=DS3231]
  Part2 = IMU Digital Combo Board 6DOF [part_number="ITGMPU ADO to vcc to change adress to ox69"]
  Grove1 = Grove OLED 128x96 [part_number=128x64]
  R1 = Resistor [tolerance=±5% resistance=10k package="0603 [SMD]"]
  R2 = Resistor [tolerance=±5% resistance=10k package=THT]
  LED1 = LED - 5mm [color="Red (633nm)" package="5 mm [THT]"]
  R3 = Resistor [tolerance=±5% resistance=670m package=THT]

nets:
  N1: Part1.D3, J1.pin3
  N2: Part1.D4, J1.pin2
  N3: Part1.A5, ZS-042_RTC1.SCL, Part2.SCL, Grove1.SCL, R1.Pin_1
  N4: Part1.A4, ZS-042_RTC1.SDA, Part2.SDA, Grove1.SDA, R2.Pin_1
  N5: Part1.A3, LED1.cathode
  GND: ZS-042_RTC1.GND, Part2.GND, Grove1.GND, R3.Pin_0
  VCC: ZS-042_RTC1.VCC, Part2.3.3V, Part2.INT1, Grove1.VCC, R1.Pin_0, R2.Pin_0
  N6: LED1.anode, R3.Pin_1
